# Fritzing sketch schematic_arduino (saved by Fritzing 0.9.3b)
breadboards: 1

parts:
  Q1 = PNP-Transistor [package="SOT-23 [SMD]"]
  R1 = Resistor [tolerance=±5% resistance=220 package=THT]
  D1 = Rectifier Diode [part_number=1N4001 package="300 mil [THT]"]
  Part1 = Arduino Nano (Rev3.0)
  BB1 = 4-Line Bi-Directional Level Shifter
  Raspberry_Pi_1 = Raspberry Pi 3 [part_number=RPI-3-V1.2]
  M1 = DC Motor

nets:
  N1: Q1.2, Part1.GND, BB1.GND#16
  N2: Q1.0, R1.Pin_0
  N3: Q1.1, D1.anode, M1.pin_2
  N4: R1.Pin_1, Part1.D3
  N5: D1.cathode, Part1.5V, BB1.HV, M1.pin_1
  N6: Part1.A5, BB1.B4
  N7: Part1.A4, BB1.B2
  N8: BB1.LV, Raspberry_Pi_1.3v3
  N9: BB1.A2, Raspberry_Pi_1.GPIO2
  N10: BB1.A4, Raspberry_Pi_1.GPIO3
  N11: BB1.GND#6, Raspberry_Pi_1.GND

custom parts:
  4-Line Bi-Directional Level Shifter: 4-Channel Bi-Directional Level Shifter
